# Fritzing sketch Sketch-Arq2 (saved by Fritzing 0.9.6b)

parts:
  NODEMCU_32S = node32s
  MAX30100 = MAX30102
  R1 = Resistor [tolerance=±5% resistance=4.7k package="1206 [SMD]"]
  DHT11 = DHT11 Humitidy and Temperature Sensor
  DS18B20 = DS18B20 1-Wire Temperature Sensor Probe Cable

nets:
  VDD: NODEMCU_32S.3.3V, MAX30100.VIN, R1.Pin_1, DHT11.VDD, DS18B20.VDD
  GND: NODEMCU_32S.GND, DS18B20.GND
  N1: NODEMCU_32S.IO22, MAX30100.SCL
  N2: NODEMCU_32S.IO21, MAX30100.SDA
  N3: NODEMCU_32S.IO19, MAX30100.INT
  N4: NODEMCU_32S.IO18, DHT11.DATA
  N5: NODEMCU_32S.IO5, R1.Pin_0, DS18B20.DQ
  GND_2: MAX30100.GND, DHT11.GND

custom parts:
  MAX30102: Oximeter module using the MAX30102 chip. You may wish to read (and check your module) this post on power problems with these modules: https://reedpaper.wordpress.com/2018/08/22/pulse-oximeter-max30100-max30102-how-to-fix-wrong-board/ . As usual, if you want the mounting holes in pcb, you need to drag a hole over the pad in silkscreen to actually drill the hole (by default they are not drilled)
  DHT11 Humitidy and Temperature Sensor: DHT11 Humidity and Temperature Sensor
